# Fritzing sketch SIDS-MonitorFritzing (saved by Fritzing 0.9.9b)
breadboards: 1

parts:
  Argon1 = Particle Argon  # not connected
  S1 = Pushbutton [package="[THT]"]
  Part1 = Passive Buzzer  # not connected
  OLED_I2C1 = OLED 128x64 I2C Monochrome Display  # not connected

nets:
  N1: S1.Pin_1, S1.Pin_2
  N2: S1.Pin_3, S1.Pin_4

custom parts:
  Particle Argon: The Argon is a powerful Wi-Fi enabled development board that can act as either a standalone Wi-Fi endpoint or Wi-Fi enabled gateway for Particle Mesh networks. It is based on the Nordic nRF52840 and has built-in battery charging circuitry so it’s easy to connect a Li-Po and deploy your local network in minutes. The Argon is great for connecting existing projects to the Particle Device Cloud or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
  Pushbutton: A generic pushbutton.
